# Fritzing sketch circuit (saved by Fritzing 0.9.3b)
breadboards: 1

parts:
  U1 = NodeMCU V1.0
  Part1 = Jtron 1 Channel Optoisolated Relay Module [package=relay]
  J1 = Piezo Speaker
  Mod2 = MQ-7 breakout
  M10 = DC Motor
  M11 = DC Motor
  BAT3 = BC9VPC [package=bc9vpc]
  IC3 = L293D [package=THT]

nets:
  N1: U1.D0, IC3.In_3
  N2: U1.D1, IC3.In_4
  N3: U1.D2, IC3.In_1
  N4: U1.D3, IC3.In_2
  N5: U1.D4, J1.pin2
  N6: U1.3V3, Part1.IN1
  GND: U1.GND, Part1.GND, J1.pin1, Mod2.GND, Mod2.AO, BAT3.V-, IC3.0V
  VCC: U1.Vin, Part1.VCC, Mod2.VCC, IC3.+V
  N7: M10.pin_1, IC3.Out_3_(_Controlled_by_Enable_2_)
  N8: M10.pin_2, IC3.Out_4_(_Controlled_by_Enable_2_)
  N9: M11.pin_1, IC3.Out_2_(_Controlled_by_Enable_1_)
  N10: M11.pin_2, IC3.Out_1_(_Controlled_by_Enable_1_)
  N11: BAT3.V+, IC3.+Vmotor

notes:
  Powersupply to drive the motor
  motors in robot chasis
  motor driver to run the motor
  Relay module
  gas sensor
  buzzer
  Nodemcu(IOT controller)

custom parts:
  NodeMCU V1.0: ESP8266 based NodeMCU
  MQ-7 breakout: MQ-5 gas sensor
