# Fritzing sketch Untitled Sketch 4 (saved by Fritzing 0.9.3b)
breadboards: 1

parts:
  LED1 = LEDs [package=led10mm]
  LED2 = LEDs [package=led10mm]
  Part1 = ACS712 Current Sensor 5A 20A 30A
  Part2 = ACS712 Current Sensor 5A 20A 30A
  S1 = Toggle Switch spst [package=THT]
  S2 = Toggle Switch spst [package=THT]
  Part3 = Lilypad Battery Connect
  Part4 = Arduino Uno (Rev3)
  U1 = ESP8266 WiFi Module [part_number=ESP8266]

nets:
  N1: LED1.A, S1.COM
  N2: LED1.C, LED2.C, Part3.-
  N3: LED2.A, Part2.1
  N4: Part1.1, S1.L1, S2.L1
  N5: Part1.2, Part1.OUT, Part3.+
  VCC: Part1.VCC, Part2.VCC, Part4.5V
  GND: Part1.GND, Part2.GND, Part4.GND, U1.GND
  N6: Part2.2, S2.COM
  N7: Part4.D0/RX, U1.TXD
  N8: Part4.D1/TX, U1.RXD
  3V3: Part4.3V3, U1.VCC, U1.CH_PD

notes:
  switch1
  switch2

custom parts:
  LEDs: LEDs Standard schematic elements and footprints for 5mm, 3mm, 1206, and 0603 sized LEDs. 5mm - Spark Fun Electronics SKU : COM-00529 (and others)
  ACS712 Current Sensor 5A 20A 30A: Remix by Michael Kubina http://www.kubina.info Original by: https://forum.fritzing.org/t/current-sensor-5a-acs712/7694 https://forum.fritzing.org/u/ArtHome ArtHome12@gmail.com
  Toggle Switch spst: Toggle Switch single pole single throw
  ESP8266 WiFi Module: Generic WiFi Module based on the ESP8266 with onboard PCB antenna and UART communications
