# Fritzing sketch smart_parking (saved by Fritzing 0.9.3b)
breadboards: 1

parts:
  U1 = NodeMCU V1.0
  PSU1 = Adjustable Breadboard Power Supply
  BAT4 = BC9VPC [package=bc9vpc]
  M1 = fc-51 [package=THT]
  M2 = fc-51 [package=THT]
  M4 = fc-51 [package=THT]
  J1 = Basic Servo
  M5 = fc-51 [package=THT]
  M3 = fc-51 [package=THT]

nets:
  N1: U1.D0, M1.pin1
  N2: U1.D1, M2.pin1
  N3: U1.D2, M3.pin1
  N4: U1.D3, M4.pin1
  N5: U1.D4, M5.pin1
  GND: U1.GND, PSU1.Vout-, M1.pin2, M2.pin2, M4.pin2, J1.gnd, M5.pin2, M3.pin2
  N6: U1.D6, J1.pulse
  N7: PSU1.Vout+, M1.pin3, M2.pin3, M4.pin3, J1.vcc, M5.pin3, M3.pin3
  N8: PSU1.Vin+, BAT4.V+
  N9: PSU1.Vin-, BAT4.V-

notes:
  Nodemcu
  IOT controller
  IR sensor for parking slot1
  IR sensor for parking slot2
  IR sensor for parking slot4
  IR sensor for parking slot3
  IR sensor for parking gate
  MB102 (external 5v power supply to power ir sensor and servo)
  Servo motor attached with gate

custom parts:
  NodeMCU V1.0: ESP8266 based NodeMCU
