# Fritzing sketch securitywithout_blink (saved by Fritzing 0.9.3b)

parts:
  PIR1 = PIR sensor
  Keypad4x1 = Keypad Membran 4x4
  Part1 = Jtron 1 Channel Optoisolated Relay Module [package=relay]
  U3 = POT [package=pot_alpha_rv16af-20]
  Part2 = Arduino Uno (Rev3) - ICSP
  U2 = LCD-16X2 [package=lcd-16x2_noholes]
  J1 = Piezo Speaker

nets:
  VDD: PIR1.VDD, Part1.VCC, U2.A
  N1: PIR1.SIG, Part2.D4
  GND: PIR1.GND, Part1.GND, U3.A, Part2.GND, U2.VSS, U2.R_W, U2.K, J1.pin1
  N2: Keypad4x1.Pin1, Part2.D6_PWM
  N3: Keypad4x1.Pin2, Part2.D7
  N4: Keypad4x1.Pin3, Part2.D8
  N5: Keypad4x1.Pin4, Part2.D9_PWM
  N6: Keypad4x1.Pin5, Part2.D10_PWM/SS
  N7: Keypad4x1.Pin6, Part2.D11_PWM/MOSI
  N8: Keypad4x1.Pin7, Part2.D12/MISO
  N9: Keypad4x1.Pin8, Part2.D13/SCK
  N10: Part1.IN1, Part2.D5_PWM
  N11: U3.S, U2.VO
  5V: U3.E, Part2.5V, U2.VDD
  N12: Part2.A0, U2.RS
  N13: Part2.A1, U2.E
  N14: Part2.A2, U2.DB4
  N15: Part2.A3, U2.DB5
  N16: Part2.A4/SDA, U2.DB6
  N17: Part2.A5/SCL, U2.DB7
  N18: Part2.D3_PWM, J1.pin2

custom parts:
  Keypad Membran 4x4: Membrane Keypad 4x4 Matrix
